// Logisim project Basic logic gates.circ as structural Verilog: 1 circuit, main circuit main
module main (
  input  A,
  input  A_2,
  input  B,
  input  B_2,
  input  A_3,
  input  A_4,
  input  B_3,
  input  B_4,
  input  A_5,
  output Y_AB,
  output Y_A_prime_B_AB_prime,
  output Y_AB_2,
  output Y_AB_A_prime_B_prime,
  output Y_A_prime
);

  and and_1 (Y_AB, A, B);
  or or_1 (Y_AB_2, A_3, B_3);
  not not_1 (Y_A_prime, A_5);
  xor xor_1 (Y_A_prime_B_AB_prime, A_2, B_2);
  xnor xnor_1 (Y_AB_A_prime_B_prime, A_4, B_4);
endmodule
